// Logisim project Logisim CPU FINAL.circ as structural Verilog: 4 circuits, main circuit CPU main
module CPU_main (
);

  wire and_1_out, and_2_out, clearmistakedata_adress_out, clearmistakeinstruction_out, Clock_out,
       controlled_inverter_1_out, input_1_blockload, input_1_clearmistakedata_addressout, input_1_clocktick,
       input_1_resetmemoryout, Instruction_Decoder_branch_always, Instruction_Decoder_branch_ne_zero,
       Instruction_Decoder_halt, Instruction_Decoder_use_immediate, Instruction_Decoder_write_acc,
       Instruction_Decoder_write_memory, isloading_out, keyboard_2_avail, loaddata_adress_out,
       loadinstruction_out, nextmemoryadress_out, not_1_out, or_1_out, or_3_out, or_4_out, or_5_out,
       or_6_out, or_7_out, previousmemoryadress_out, Reset_out, resetmemory_out;
  wire [3:0] input_1_data_adresstoloadcounter, input_1_data_adresstoloadcounter_2,
       input_1_memoryaddresscounter, input_1_memoryaddresscounter_2, Instruction_Decoder_alu_operation;
  wire [6:0] input_1_consoleoutput, keyboard_1_data, keyboard_2_data;
  wire [7:0] ACC_q, adder_1_out, ALU_alu_out_to_acc, input_1_adressinram,
       Instruction_Decoder_address_or_immediate, multiplexer_1_out, multiplexer_2_out, or_2_out, PC_q,
       ram_2_data;
  wire [8:7] input_1_consoleoutput_2;
  wire [15:0] input_1_datainram, ram_1_data;

  Clock isloading (.out(isloading_out));
  Button resetmemory (.out(resetmemory_out));
  Clock loaddata_adress (.out(loaddata_adress_out));
  Keyboard keyboard_1 (
    .clk(loaddata_adress_out), .clr(input_1_clearmistakedata_addressout), .data(keyboard_1_data));  // open: re, avail
  Button clearmistakedata_adress (.out(clearmistakedata_adress_out));
  Hex_Digit_Display hex_digit_display_1 (.value(input_1_data_adresstoloadcounter_2));  // open: dp
  Button nextmemoryadress (.out(nextmemoryadress_out));
  Button previousmemoryadress (.out(previousmemoryadress_out));
  Hex_Digit_Display hex_digit_display_2 (.value(input_1_memoryaddresscounter_2));  // open: dp
  Clock loadinstruction (.out(loadinstruction_out));
  Keyboard keyboard_2 (
    .clk(loadinstruction_out), .clr(clearmistakeinstruction_out), .avail(keyboard_2_avail),
    .data(keyboard_2_data));  // open: re
  Button clearmistakeinstruction (.out(clearmistakeinstruction_out));
  TTY tty_1 (
    .data(input_1_consoleoutput), .clk(input_1_consoleoutput_2[7]), .clr(input_1_consoleoutput_2[8]));  // open: we
  Hex_Digit_Display hex_digit_display_3 (.value(input_1_data_adresstoloadcounter));  // open: dp
  Hex_Digit_Display hex_digit_display_4 (.value(input_1_memoryaddresscounter));  // open: dp
  or or_1 (or_1_out, resetmemory_out, Reset_out);
  Input input_1 (
    .loaddata_address(keyboard_1_data), .loaddata_addresstick(loaddata_adress_out),
    .clearmistakedata_address(clearmistakedata_adress_out), .instructionhasvalue(keyboard_2_avail),
    .loadinstruction(keyboard_2_data), .previousmemoryadress(previousmemoryadress_out),
    .nextmemoryadress(nextmemoryadress_out), .loadinstruction_2(loadinstruction_out),
    .clearmistakeinstruction(clearmistakeinstruction_out), .isloading(isloading_out),
    .resetmemoryin(or_1_out), .clearmistakedata_addressout(input_1_clearmistakedata_addressout),
    .data_adresstoloadcounter({input_1_data_adresstoloadcounter_2, input_1_data_adresstoloadcounter}),
    .memoryaddresscounter({input_1_memoryaddresscounter_2, input_1_memoryaddresscounter}),
    .adressinram(input_1_adressinram), .datainram(input_1_datainram),
    .resetmemoryout(input_1_resetmemoryout), .clocktick(input_1_clocktick), .blockload(input_1_blockload),
    .consoleoutput({input_1_consoleoutput_2, input_1_consoleoutput}));
  assign or_2_out = PC_q | input_1_adressinram;  // OR_Gate or_2, 8 bits wide
  or or_3 (or_3_out, isloading_out, 1'b0);
  Adder adder_1 (.a(PC_q), .b(8'h1), .out(adder_1_out));  // open: cin, cout
  Multiplexer #(.width(8)) multiplexer_1 (
    .in0(adder_1_out), .in1(Instruction_Decoder_address_or_immediate), .out(multiplexer_1_out), .sel(or_4_out));  // open: en
  or or_4 (or_4_out, and_1_out, Instruction_Decoder_branch_always);
  or or_5 (or_5_out, ACC_q[7], ACC_q[6], ACC_q[5], ACC_q[4], ACC_q[3], ACC_q[2], ACC_q[1], ACC_q[0]);
  or or_6 (or_6_out, input_1_clocktick, and_2_out);
  assign controlled_inverter_1_out = input_1_blockload ? ~1'b0 : 1'bz;  // Controlled_Inverter controlled_inverter_1
  Register PC (.D(multiplexer_1_out), .en(1'b1), .Q(PC_q), .clk(and_2_out), .clr(Reset_out));
  RAM #(.dataWidth(16), .bus("separate")) ram_1 (
    .addr(or_2_out), .din(input_1_datainram), .data(ram_1_data), .str(or_3_out),
    .sel(controlled_inverter_1_out), .clk(or_6_out), .clr(or_7_out));  // open: ld
  or or_7 (or_7_out, input_1_resetmemoryout, Reset_out);
  Clock Clock (.out(Clock_out));
  Button Reset (.out(Reset_out));
  and and_1 (and_1_out, Instruction_Decoder_branch_ne_zero, or_5_out);
  Instruction_Decoding_Unit Instruction_Decoder (
    .Instruction(ram_1_data), .Address_or_Immediate(Instruction_Decoder_address_or_immediate),
    .Write_Memory(Instruction_Decoder_write_memory), .Use_Immediate(Instruction_Decoder_use_immediate),
    .ALU_Operation(Instruction_Decoder_alu_operation), .Write_ACC(Instruction_Decoder_write_acc),
    .Branch_always(Instruction_Decoder_branch_always), .Branch_NE_zero(Instruction_Decoder_branch_ne_zero),
    .Halt(Instruction_Decoder_halt));
  not not_1 (not_1_out, Instruction_Decoder_halt);
  and and_2 (and_2_out, not_1_out, Clock_out);
  RAM #(.bus("separate")) ram_2 (
    .addr(Instruction_Decoder_address_or_immediate), .din(ACC_q), .data(ram_2_data),
    .str(Instruction_Decoder_write_memory), .clk(and_2_out), .clr(Reset_out));  // open: sel, ld
  Multiplexer #(.width(8)) multiplexer_2 (
    .in0(ram_2_data), .in1(Instruction_Decoder_address_or_immediate), .out(multiplexer_2_out),
    .sel(Instruction_Decoder_use_immediate));  // open: en
  ALU ALU (
    .ACC_to_ALU(ACC_q), .Inp_to_ALU(multiplexer_2_out), .ALU_Operation(Instruction_Decoder_alu_operation),
    .ALU_out_to_ACC(ALU_alu_out_to_acc));  // open: Not_Equal_Zero
  Register ACC (
    .D(ALU_alu_out_to_acc), .en(Instruction_Decoder_write_acc), .Q(ACC_q), .clk(and_2_out), .clr(Reset_out));

  // Notes on the sheet:
  //   data/adresstoload
  //   loadeddata/adress
  //   loadedinstruction
  //   istructiontoload
  //   Add 1
  //   Student id: 21330134
  //   Program memory
  //   Data memory
  //   Output from data memory
  //   SELECT
  //   Output from ACC
endmodule

module ALU (
  input  [7:0] ACC_to_ALU,
  input  [7:0] Inp_to_ALU,
  input  [3:0] ALU_Operation,
  output [7:0] ALU_out_to_ACC,
  output [7:0] Not_Equal_Zero
);

  wire [7:0] adder_1_out, divider_1_p3, multiplier_1_out, not_1_out, subtractor_1_out, xor_1_out;

  Adder adder_1 (.a(ACC_to_ALU), .b(Inp_to_ALU), .out(adder_1_out));  // open: cin, cout
  assign xor_1_out = ACC_to_ALU ^ Inp_to_ALU;  // XOR_Gate xor_1, 8 bits wide
  Multiplier multiplier_1 (.a(ACC_to_ALU), .b(Inp_to_ALU), .out(multiplier_1_out));  // open: cin, cout
  assign not_1_out = ~ACC_to_ALU;  // NOT_Gate not_1, 8 bits wide
  Subtractor subtractor_1 (.a(ACC_to_ALU), .b(Inp_to_ALU), .out(subtractor_1_out));  // open: bin, bout
  // Divider divider_1: pin names not known; wires that end beside it: ACC_to_ALU, Inp_to_ALU, divider_1_p3
  Multiplexer #(.select(4), .width(8)) multiplexer_1 (
    .in0(Inp_to_ALU), .in1(adder_1_out), .in2(xor_1_out), .in3(multiplier_1_out), .in4(not_1_out),
    .in5(subtractor_1_out), .in6(divider_1_p3), .out(ALU_out_to_ACC), .sel(ALU_Operation));  // open: in7, in8, in9, in10, in11, in12, in13, in14, in15, en

  assign Not_Equal_Zero = {8{1'b0}};
endmodule

module Instruction_Decoding_Unit (
  input  [15:0] Instruction,
  output [7:0] Address_or_Immediate,
  output Write_Memory,
  output Use_Immediate,
  output [3:0] ALU_Operation,
  output Write_ACC,
  output Branch_always,
  output Branch_NE_zero,
  output Halt
);

  wire decoder_1_out2;

  Decoder #(.select(4)) decoder_1 (
    .out1(Use_Immediate), .out2(decoder_1_out2), .out3(Write_Memory), .out4(Branch_always),
    .out5(Branch_NE_zero), .out15(Halt), .sel(Instruction[15:12]));  // open: out0, out6, out7, out8, out9, out10, out11, out12, out13, out14, en
  or or_1 (Write_ACC, Use_Immediate, decoder_1_out2);

  assign Address_or_Immediate = Instruction[7:0];
  assign ALU_Operation = Instruction[11:8];
endmodule

module Input (
  input  [6:0] loaddata_address,
  input  loaddata_addresstick,
  input  clearmistakedata_address,
  input  instructionhasvalue,
  input  [6:0] loadinstruction,
  input  previousmemoryadress,
  input  nextmemoryadress,
  input  loadinstruction_2,
  input  clearmistakeinstruction,
  input  isloading,
  input  resetmemoryin,
  output clearmistakedata_addressout,
  output [7:0] data_adresstoloadcounter,
  output [7:0] memoryaddresscounter,
  output [7:0] adressinram,
  output [15:0] datainram,
  output resetmemoryout,
  output clocktick,
  output blockload,
  output [8:0] consoleoutput
);

  wire comparator_1_gt, not_1_out, or_3_out, or_4_out;
  wire [3:0] bit_extender_2_out;
  wire [6:0] controlled_buffer_1_out, register_3_q, subtractor_1_out;
  wire [7:0] adder_1_out, bit_extender_1_out, register_4_q;

  Hex_Digit_Display hex_digit_display_1 (.value(adressinram[7:4]));  // open: dp
  or or_1 (clearmistakedata_addressout, clearmistakedata_address, previousmemoryadress, nextmemoryadress);
  Hex_Digit_Display hex_digit_display_2 (.value(adressinram[3:0]));  // open: dp
  Register #(.width(4)) register_1 (
    .D(data_adresstoloadcounter[3:0]), .Q(data_adresstoloadcounter[7:4]), .clk(loaddata_addresstick),
    .clr(clearmistakedata_addressout));  // open: en
  Hex_Digit_Display hex_digit_display_3 (.value(data_adresstoloadcounter[7:4]));  // open: dp
  or or_2 (consoleoutput[8], clearmistakeinstruction, nextmemoryadress, previousmemoryadress);
  Register #(.width(4)) register_2 (
    .D(bit_extender_2_out), .Q(data_adresstoloadcounter[3:0]), .clk(loaddata_addresstick),
    .clr(clearmistakedata_addressout));  // open: en
  Hex_Digit_Display hex_digit_display_4 (.value(data_adresstoloadcounter[3:0]));  // open: dp
  TTY tty_1 (.data(loadinstruction), .clk(loadinstruction_2), .clr(consoleoutput[8]));  // open: we
  assign bit_extender_1_out = {{1{1'b0}}, loadinstruction};  // Bit_Extender bit_extender_1
  or or_3 (or_3_out, nextmemoryadress, previousmemoryadress, clearmistakeinstruction);
  Subtractor #(.width(7)) subtractor_1 (
    .a(loaddata_address), .b(7'b0110000), .out(subtractor_1_out));  // open: bin, bout
  Register #(.width(7)) register_3 (
    .D(controlled_buffer_1_out), .Q(register_3_q), .clk(loaddata_addresstick),
    .clr(clearmistakedata_addressout));  // open: en
  Register register_4 (.D(adder_1_out), .Q(register_4_q), .clk(loadinstruction_2), .clr(or_3_out));  // open: en
  Comparator #(.width(7), .mode("unsigned")) comparator_1 (
    .a(7'b0001010), .b(subtractor_1_out), .gt(comparator_1_gt));  // open: eq, lt
  assign controlled_buffer_1_out = comparator_1_gt ? subtractor_1_out : 7'bz;  // Controlled_Buffer controlled_buffer_1
  Bit_Extender #(.in_width(7), .out_width(4)) bit_extender_2 (.in(register_3_q), .out(bit_extender_2_out));
  Adder adder_1 (.a(bit_extender_1_out), .b(register_4_q), .out(adder_1_out));  // open: cin, cout
  assign blockload = not_1_out ? ~instructionhasvalue : 1'bz;  // Controlled_Inverter controlled_inverter_1
  not not_1 (not_1_out, clearmistakeinstruction);
  or or_4 (or_4_out, previousmemoryadress, nextmemoryadress);
  ROM rom_1 (.addr(register_4_q), .data(datainram[15:8]));  // open: sel
  Counter counter_1 (
    .load(previousmemoryadress), .count(1'b1), .Q(adressinram), .clk(or_4_out), .clr(resetmemoryin));  // open: D, carry
  RAM #(.dataWidth(16), .bus("separate")) ram_1 (
    .addr(adressinram), .din({datainram[15:8], data_adresstoloadcounter}), .str(isloading), .sel(blockload),
    .clk(loadinstruction_2), .clr(resetmemoryin));  // open: data, ld

  assign clocktick = loadinstruction_2;
  assign consoleoutput[7:0] = {loadinstruction_2, loadinstruction};
  assign datainram[7:0] = data_adresstoloadcounter;
  assign memoryaddresscounter = adressinram;
  assign resetmemoryout = resetmemoryin;

  // Notes on the sheet:
  //   current memory adress in hex
  //   data or memory value in base 10
  //   contents of rom_1 (hex, n*v repeats v):
  //   41*0 21 0 23 8*0 50 14*0 26 13*0 24 7*0 22 39*0 10 30*0 20 4*0 25 20*0 40 11*0 f0
endmodule
